// Logisim project Add16.circ as structural Verilog: 1 circuit, main circuit main
module main (
  input  [15:0] a,
  input  [15:0] b,
  input  cin,
  output [15:0] out
);

  Adder #(.width(16)) adder_1 (.a(a), .b(b), .out(out));  // open: cin, cout
endmodule
