// Logisim project DMux4way.circ as structural Verilog: 17 circuits, main circuit DMux4way
module Mux4to1 (
  input  in_1,
  input  in_2,
  input  in_3,
  input  in_4,
  input  in_5,
  input  in_6,
  output out_7
);

  wire and_1_out, and_2_out, and_3_out, and_4_out, not_1_out, not_2_out;

  not not_1 (not_1_out, in_5);
  not not_2 (not_2_out, in_6);
  and and_1 (and_1_out, in_1, in_5, in_6);
  and and_2 (and_2_out, in_2, not_1_out, in_6);
  and and_3 (and_3_out, in_3, not_2_out, in_5);
  and and_4 (and_4_out, in_4, not_1_out, not_2_out);
  or or_1 (out_7, and_1_out, and_2_out, and_3_out, and_4_out);
endmodule

module Mux8Bits (
  input  in_1,
  input  in_2,
  input  in_3,
  input  in_4,
  input  in_5,
  input  in_6,
  input  [2:0] in_7,
  input  in_8,
  input  in_9,
  output out_10
);

  Multiplexer #(.select(3), .enable("false")) multiplexer_1 (
    .in0(in_1), .in1(in_2), .in2(in_3), .in3(in_4), .in4(in_5), .in5(in_6), .in6(in_8), .in7(in_9),
    .out(out_10), .sel(in_7));
endmodule

module DMux4way (
  input  in,
  input  [1:0] sel,
  output a,
  output b,
  output c,
  output d
);

  Demultiplexer #(.select(2), .enable("false")) demultiplexer_1 (
    .out0(a), .out1(b), .out2(c), .out3(d), .in(in), .sel(sel));

  // Notes on the sheet:
  //   DMux4way
endmodule

module DMux8Way (
  input  in,
  input  [2:0] sel,
  output a,
  output b,
  output c,
  output d,
  output e,
  output f,
  output g,
  output h
);

  Demultiplexer #(.select(3), .enable("false")) demultiplexer_1 (
    .out0(a), .out1(b), .out2(c), .out3(d), .out4(e), .out5(f), .out6(g), .out7(h), .in(in), .sel(sel));

  // Notes on the sheet:
  //   DMux8way
  //   a = 0 0 0, b = 0 0 1
  //   c = 0 1 0 , d = 0 1 1
  //   e = 1 0 0, f = 1 0 1
  //   g = 1 1 0 , h = 1 1 1
endmodule

module Sum_Carry (
  input  a,
  input  b,
  output Sum,
  output Carry
);

  xor xor_1 (Sum, a, b);
  and and_1 (Carry, a, b);
endmodule

module SumadorCompleto (
  input  a,
  input  b,
  input  Cin,
  output Sum,
  output Cout
);

  wire and_1_out, and_2_out, xor_1_out;

  xor xor_1 (xor_1_out, a, b);
  and and_1 (and_1_out, Cin, xor_1_out);
  and and_2 (and_2_out, a, b);
  or or_1 (Cout, and_1_out, and_2_out);
  xor xor_2 (Sum, xor_1_out, Cin);
endmodule

module SumadorCuatroBits (
  input  A3,
  input  B3,
  input  A2,
  input  B2,
  input  A1,
  input  B1,
  input  A0,
  input  B0,
  output Sum3,
  output Sum2,
  output Sum1,
  output Sum0,
  output Cout
);

  wire sum_carry_1_carry, sumadorcompleto_2_cout, sumadorcompleto_3_cout;

  SumadorCompleto sumadorcompleto_1 (.a(A3), .b(B3), .Cin(sumadorcompleto_2_cout), .Sum(Sum3), .Cout(Cout));
  SumadorCompleto sumadorcompleto_2 (
    .a(A2), .b(B2), .Cin(sumadorcompleto_3_cout), .Sum(Sum2), .Cout(sumadorcompleto_2_cout));
  SumadorCompleto sumadorcompleto_3 (
    .a(A1), .b(B1), .Cin(sum_carry_1_carry), .Sum(Sum1), .Cout(sumadorcompleto_3_cout));
  Sum_Carry sum_carry_1 (.a(A0), .b(B0), .Sum(Sum0), .Carry(sum_carry_1_carry));
endmodule

module Sumador16Bits (
  input  B3,
  input  A3,
  input  B2,
  input  A2,
  input  B1,
  input  A1,
  input  B0,
  input  A0,
  input  B4,
  input  A4,
  input  B5,
  input  A5,
  input  B6,
  input  A6,
  input  B7,
  input  A7,
  input  B11,
  input  A11,
  input  B10,
  input  A10,
  input  B9,
  input  A9,
  input  B8,
  input  A8,
  input  B12,
  input  A12,
  input  B13,
  input  A13,
  input  B14,
  input  A14,
  input  B15,
  input  A15,
  output Sum3,
  output Sum2,
  output Sum1,
  output Sum0,
  output Sum4,
  output Sum5,
  output Sum6,
  output Sum7,
  output Sum11,
  output Sum10,
  output Sum9,
  output Sum8,
  output Sum12,
  output Sum13,
  output Sum14,
  output Sum15,
  output Cout
);

  wire sum_carry_1_carry, sumadorcompleto_1_cout, sumadorcompleto_2_cout, sumadorcompleto_3_cout,
       sumadorcompleto_4_cout, sumadorcompleto_5_cout, sumadorcompleto_6_cout, sumadorcompleto_7_cout,
       sumadorcompleto_8_cout, sumadorcompleto_9_cout, sumadorcompleto_10_cout, sumadorcompleto_11_cout,
       sumadorcompleto_12_cout, sumadorcompleto_13_cout, sumadorcompleto_14_cout;

  SumadorCompleto sumadorcompleto_1 (
    .a(A3), .b(B3), .Cin(sumadorcompleto_5_cout), .Sum(Sum3), .Cout(sumadorcompleto_1_cout));
  SumadorCompleto sumadorcompleto_2 (
    .a(B4), .b(A4), .Cin(sumadorcompleto_1_cout), .Sum(Sum4), .Cout(sumadorcompleto_2_cout));
  SumadorCompleto sumadorcompleto_3 (
    .a(A11), .b(B11), .Cin(sumadorcompleto_7_cout), .Sum(Sum11), .Cout(sumadorcompleto_3_cout));
  SumadorCompleto sumadorcompleto_4 (
    .a(A12), .b(B12), .Cin(sumadorcompleto_3_cout), .Sum(Sum12), .Cout(sumadorcompleto_4_cout));
  SumadorCompleto sumadorcompleto_5 (
    .a(A2), .b(B2), .Cin(sumadorcompleto_9_cout), .Sum(Sum2), .Cout(sumadorcompleto_5_cout));
  SumadorCompleto sumadorcompleto_6 (
    .a(B5), .b(A5), .Cin(sumadorcompleto_2_cout), .Sum(Sum5), .Cout(sumadorcompleto_6_cout));
  SumadorCompleto sumadorcompleto_7 (
    .a(A10), .b(B10), .Cin(sumadorcompleto_11_cout), .Sum(Sum10), .Cout(sumadorcompleto_7_cout));
  SumadorCompleto sumadorcompleto_8 (
    .a(A13), .b(B13), .Cin(sumadorcompleto_4_cout), .Sum(Sum13), .Cout(sumadorcompleto_8_cout));
  SumadorCompleto sumadorcompleto_9 (
    .a(A1), .b(B1), .Cin(sum_carry_1_carry), .Sum(Sum1), .Cout(sumadorcompleto_9_cout));
  SumadorCompleto sumadorcompleto_10 (
    .a(B6), .b(A6), .Cin(sumadorcompleto_6_cout), .Sum(Sum6), .Cout(sumadorcompleto_10_cout));
  SumadorCompleto sumadorcompleto_11 (
    .a(A9), .b(B9), .Cin(sumadorcompleto_14_cout), .Sum(Sum9), .Cout(sumadorcompleto_11_cout));
  SumadorCompleto sumadorcompleto_12 (
    .a(A14), .b(B14), .Cin(sumadorcompleto_8_cout), .Sum(Sum14), .Cout(sumadorcompleto_12_cout));
  Sum_Carry sum_carry_1 (.a(A0), .b(B0), .Sum(Sum0), .Carry(sum_carry_1_carry));
  SumadorCompleto sumadorcompleto_13 (
    .a(B7), .b(A7), .Cin(sumadorcompleto_10_cout), .Sum(Sum7), .Cout(sumadorcompleto_13_cout));
  SumadorCompleto sumadorcompleto_14 (
    .a(A8), .b(B8), .Cin(sumadorcompleto_13_cout), .Sum(Sum8), .Cout(sumadorcompleto_14_cout));
  SumadorCompleto sumadorcompleto_15 (.a(A15), .b(B15), .Cin(sumadorcompleto_12_cout), .Sum(Sum15), .Cout(Cout));
endmodule

module Sumador16bits (
  input  [15:0] A,
  input  [15:0] B,
  output [15:0] Sum,
  output Cout
);

  wire sum_carry_1_carry, sumadorcompleto_1_cout, sumadorcompleto_2_cout, sumadorcompleto_3_cout,
       sumadorcompleto_4_cout, sumadorcompleto_5_cout, sumadorcompleto_6_cout, sumadorcompleto_7_cout,
       sumadorcompleto_8_cout, sumadorcompleto_9_cout, sumadorcompleto_10_cout, sumadorcompleto_11_cout,
       sumadorcompleto_12_cout, sumadorcompleto_13_cout, sumadorcompleto_14_cout;

  SumadorCompleto sumadorcompleto_1 (
    .a(A[13]), .b(B[13]), .Cin(sumadorcompleto_4_cout), .Sum(Sum[13]), .Cout(sumadorcompleto_1_cout));
  SumadorCompleto sumadorcompleto_2 (
    .a(A[4]), .b(B[4]), .Cin(sumadorcompleto_5_cout), .Sum(Sum[4]), .Cout(sumadorcompleto_2_cout));
  SumadorCompleto sumadorcompleto_3 (
    .a(A[5]), .b(B[5]), .Cin(sumadorcompleto_2_cout), .Sum(Sum[5]), .Cout(sumadorcompleto_3_cout));
  SumadorCompleto sumadorcompleto_4 (
    .a(A[12]), .b(B[12]), .Cin(sumadorcompleto_7_cout), .Sum(Sum[12]), .Cout(sumadorcompleto_4_cout));
  SumadorCompleto sumadorcompleto_5 (
    .a(A[3]), .b(B[3]), .Cin(sumadorcompleto_8_cout), .Sum(Sum[3]), .Cout(sumadorcompleto_5_cout));
  SumadorCompleto sumadorcompleto_6 (
    .a(A[6]), .b(B[6]), .Cin(sumadorcompleto_3_cout), .Sum(Sum[6]), .Cout(sumadorcompleto_6_cout));
  SumadorCompleto sumadorcompleto_7 (
    .a(A[11]), .b(B[11]), .Cin(sumadorcompleto_10_cout), .Sum(Sum[11]), .Cout(sumadorcompleto_7_cout));
  SumadorCompleto sumadorcompleto_8 (
    .a(A[2]), .b(B[2]), .Cin(sumadorcompleto_12_cout), .Sum(Sum[2]), .Cout(sumadorcompleto_8_cout));
  SumadorCompleto sumadorcompleto_9 (
    .a(A[7]), .b(B[7]), .Cin(sumadorcompleto_6_cout), .Sum(Sum[7]), .Cout(sumadorcompleto_9_cout));
  SumadorCompleto sumadorcompleto_10 (
    .a(A[10]), .b(B[10]), .Cin(sumadorcompleto_14_cout), .Sum(Sum[10]), .Cout(sumadorcompleto_10_cout));
  SumadorCompleto sumadorcompleto_11 (
    .a(A[14]), .b(B[14]), .Cin(sumadorcompleto_1_cout), .Sum(Sum[14]), .Cout(sumadorcompleto_11_cout));
  SumadorCompleto sumadorcompleto_12 (
    .a(A[1]), .b(B[1]), .Cin(sum_carry_1_carry), .Sum(Sum[1]), .Cout(sumadorcompleto_12_cout));
  SumadorCompleto sumadorcompleto_13 (
    .a(A[8]), .b(B[8]), .Cin(sumadorcompleto_9_cout), .Sum(Sum[8]), .Cout(sumadorcompleto_13_cout));
  SumadorCompleto sumadorcompleto_14 (
    .a(A[9]), .b(B[9]), .Cin(sumadorcompleto_13_cout), .Sum(Sum[9]), .Cout(sumadorcompleto_14_cout));
  SumadorCompleto sumadorcompleto_15 (.a(A[15]), .b(B[15]), .Cin(sumadorcompleto_11_cout), .Sum(Sum[15]), .Cout(Cout));
  Sum_Carry sum_carry_1 (.a(A[0]), .b(B[0]), .Sum(Sum[0]), .Carry(sum_carry_1_carry));
endmodule

module Incrementador16Bits (
  input  [15:0] A,
  output [15:0] Out,
  output Cout
);

  Sumador16bits sumador16bits_1 (.A(A), .B(16'h1), .Sum(Out), .Cout(Cout));
endmodule

module DFlipFlop (
  input  Set,
  output Q
);

  wire and_1_out, clock_1_out, nand_1_out;

  Clock clock_1 (.out(clock_1_out));
  and and_1 (and_1_out, Set, clock_1_out);
  nand nand_1 (nand_1_out, and_1_out, Q);
  nand nand_2 (Q, nand_1_out, and_1_out);
endmodule

// 16BR
module _16BitRegister (
  input  clock,
  input  [15:0] In,
  input  load,
  output [15:0] Out
);

  D_Flip_Flop d_ff_1 (.clk(clock), .D(In[0]), .Q(Out[0]), .en(load));  // open: Qn, preset, reset
  D_Flip_Flop d_ff_2 (.clk(clock), .D(In[4]), .Q(Out[4]), .en(load));  // open: Qn, preset, reset
  D_Flip_Flop d_ff_3 (.clk(clock), .D(In[8]), .Q(Out[8]), .en(load));  // open: Qn, preset, reset
  D_Flip_Flop d_ff_4 (.clk(clock), .D(In[12]), .Q(Out[12]), .en(load));  // open: Qn, preset, reset
  D_Flip_Flop d_ff_5 (.clk(clock), .D(In[1]), .Q(Out[1]), .en(load));  // open: Qn, preset, reset
  D_Flip_Flop d_ff_6 (.clk(clock), .D(In[5]), .Q(Out[5]), .en(load));  // open: Qn, preset, reset
  D_Flip_Flop d_ff_7 (.clk(clock), .D(In[9]), .Q(Out[9]), .en(load));  // open: Qn, preset, reset
  D_Flip_Flop d_ff_8 (.clk(clock), .D(In[13]), .Q(Out[13]), .en(load));  // open: Qn, preset, reset
  D_Flip_Flop d_ff_9 (.clk(clock), .D(In[2]), .Q(Out[2]), .en(load));  // open: Qn, preset, reset
  D_Flip_Flop d_ff_10 (.clk(clock), .D(In[6]), .Q(Out[6]), .en(load));  // open: Qn, preset, reset
  D_Flip_Flop d_ff_11 (.clk(clock), .D(In[10]), .Q(Out[10]), .en(load));  // open: Qn, preset, reset
  D_Flip_Flop d_ff_12 (.clk(clock), .D(In[14]), .Q(Out[14]), .en(load));  // open: Qn, preset, reset
  D_Flip_Flop d_ff_13 (.clk(clock), .D(In[3]), .Q(Out[3]), .en(load));  // open: Qn, preset, reset
  D_Flip_Flop d_ff_14 (.clk(clock), .D(In[7]), .Q(Out[7]), .en(load));  // open: Qn, preset, reset
  D_Flip_Flop d_ff_15 (.clk(clock), .D(In[11]), .Q(Out[11]), .en(load));  // open: Qn, preset, reset
  D_Flip_Flop d_ff_16 (.clk(clock), .D(In[15]), .Q(Out[15]), .en(load));  // open: Qn, preset, reset

  // Other names for the same wires on the sheet: Reloj = clock
endmodule

module RAM8 (
  input  [15:0] In,
  input  Clock,
  input  [2:0] adress,
  input  load,
  output [15:0] Out
);

  wire dmux8way_1_a, dmux8way_1_b, dmux8way_1_c, dmux8way_1_d, dmux8way_1_e, dmux8way_1_f, dmux8way_1_g,
       dmux8way_1_h;
  wire [15:0] n16bitregister_1_out, n16bitregister_2_out, n16bitregister_3_out, n16bitregister_4_out,
       n16bitregister_5_out, n16bitregister_6_out, n16bitregister_7_out, n16bitregister_8_out;

  DMux8Way dmux8way_1 (
    .in(load), .sel(adress), .a(dmux8way_1_a), .b(dmux8way_1_b), .c(dmux8way_1_c), .d(dmux8way_1_d),
    .e(dmux8way_1_e), .f(dmux8way_1_f), .g(dmux8way_1_g), .h(dmux8way_1_h));
  _16BitRegister u_16bitregister_1 (.clock(Clock), .load(dmux8way_1_a), .Out(n16bitregister_1_out), .In(In));
  _16BitRegister u_16bitregister_2 (.clock(Clock), .load(dmux8way_1_b), .Out(n16bitregister_2_out), .In(In));
  _16BitRegister u_16bitregister_3 (.clock(Clock), .load(dmux8way_1_c), .Out(n16bitregister_3_out), .In(In));
  _16BitRegister u_16bitregister_4 (.clock(Clock), .load(dmux8way_1_d), .Out(n16bitregister_4_out), .In(In));
  _16BitRegister u_16bitregister_5 (.clock(Clock), .load(dmux8way_1_e), .Out(n16bitregister_5_out), .In(In));
  _16BitRegister u_16bitregister_6 (.clock(Clock), .load(dmux8way_1_f), .Out(n16bitregister_6_out), .In(In));
  _16BitRegister u_16bitregister_7 (.clock(Clock), .load(dmux8way_1_g), .Out(n16bitregister_7_out), .In(In));
  _16BitRegister u_16bitregister_8 (.clock(Clock), .load(dmux8way_1_h), .Out(n16bitregister_8_out), .In(In));
  Multiplexer #(.select(3), .width(16), .enable("false")) multiplexer_1 (
    .in0(n16bitregister_1_out), .in1(n16bitregister_2_out), .in2(n16bitregister_3_out),
    .in3(n16bitregister_4_out), .in4(n16bitregister_5_out), .in5(n16bitregister_6_out),
    .in6(n16bitregister_7_out), .in7(n16bitregister_8_out), .out(Out), .sel(adress));
endmodule

module RAM64 (
  input  [15:0] In,
  input  Clock,
  input  [5:0] adress,
  input  load,
  output [15:0] Out
);

  wire dmux8way_1_a, dmux8way_1_b, dmux8way_1_c, dmux8way_1_d, dmux8way_1_e, dmux8way_1_f, dmux8way_1_g,
       dmux8way_1_h;
  wire [15:0] ram8_1_out, ram8_2_out, ram8_3_out, ram8_4_out, ram8_5_out, ram8_6_out, ram8_7_out, ram8_8_out;

  DMux8Way dmux8way_1 (
    .in(load), .sel(adress[5:3]), .a(dmux8way_1_a), .b(dmux8way_1_b), .c(dmux8way_1_c), .d(dmux8way_1_d),
    .e(dmux8way_1_e), .f(dmux8way_1_f), .g(dmux8way_1_g), .h(dmux8way_1_h));
  RAM8 ram8_1 (.In(In), .Clock(Clock), .adress(adress[2:0]), .load(dmux8way_1_a), .Out(ram8_1_out));
  RAM8 ram8_2 (.In(In), .Clock(Clock), .adress(adress[2:0]), .load(dmux8way_1_b), .Out(ram8_2_out));
  RAM8 ram8_3 (.In(In), .Clock(Clock), .adress(adress[2:0]), .load(dmux8way_1_c), .Out(ram8_3_out));
  RAM8 ram8_4 (.In(In), .Clock(Clock), .adress(adress[2:0]), .load(dmux8way_1_d), .Out(ram8_4_out));
  RAM8 ram8_5 (.In(In), .Clock(Clock), .adress(adress[2:0]), .load(dmux8way_1_e), .Out(ram8_5_out));
  RAM8 ram8_6 (.In(In), .Clock(Clock), .adress(adress[2:0]), .load(dmux8way_1_f), .Out(ram8_6_out));
  RAM8 ram8_7 (.In(In), .Clock(Clock), .adress(adress[2:0]), .load(dmux8way_1_g), .Out(ram8_7_out));
  RAM8 ram8_8 (.In(In), .Clock(Clock), .adress(adress[2:0]), .load(dmux8way_1_h), .Out(ram8_8_out));
  Multiplexer #(.select(3), .width(16), .enable("false")) multiplexer_1 (
    .in0(ram8_1_out), .in1(ram8_2_out), .in2(ram8_3_out), .in3(ram8_4_out), .in4(ram8_5_out),
    .in5(ram8_6_out), .in6(ram8_7_out), .in7(ram8_8_out), .out(Out), .sel(adress[5:3]));

  // Other names for the same wires on the sheet: adress_t[2:0] = adress[2:0]; adress1[2:0] = adress[5:3]
endmodule

module RAM512 (
  input  [15:0] In,
  input  in_2,
  input  [8:0] address,
  input  load,
  output [15:0] Out
);

  wire dmux8way_1_a, dmux8way_1_b, dmux8way_1_c, dmux8way_1_d, dmux8way_1_e, dmux8way_1_f, dmux8way_1_g,
       dmux8way_1_h;
  wire [15:0] ram64_1_out, ram64_2_out, ram64_3_out, ram64_4_out, ram64_5_out, ram64_6_out, ram64_7_out,
       ram64_8_out;

  DMux8Way dmux8way_1 (
    .in(load), .sel(address[8:6]), .a(dmux8way_1_a), .b(dmux8way_1_b), .c(dmux8way_1_c), .d(dmux8way_1_d),
    .e(dmux8way_1_e), .f(dmux8way_1_f), .g(dmux8way_1_g), .h(dmux8way_1_h));
  RAM64 ram64_1 (.In(In), .Clock(in_2), .adress(address[5:0]), .load(dmux8way_1_a), .Out(ram64_1_out));
  RAM64 ram64_2 (.In(In), .Clock(in_2), .adress(address[5:0]), .load(dmux8way_1_b), .Out(ram64_2_out));
  RAM64 ram64_3 (.In(In), .Clock(in_2), .adress(address[5:0]), .load(dmux8way_1_c), .Out(ram64_3_out));
  RAM64 ram64_4 (.In(In), .Clock(in_2), .adress(address[5:0]), .load(dmux8way_1_d), .Out(ram64_4_out));
  RAM64 ram64_5 (.In(In), .Clock(in_2), .adress(address[5:0]), .load(dmux8way_1_e), .Out(ram64_5_out));
  RAM64 ram64_6 (.In(In), .Clock(in_2), .adress(address[5:0]), .load(dmux8way_1_f), .Out(ram64_6_out));
  RAM64 ram64_7 (.In(In), .Clock(in_2), .adress(address[5:0]), .load(dmux8way_1_g), .Out(ram64_7_out));
  RAM64 ram64_8 (.In(In), .Clock(in_2), .adress(address[5:0]), .load(dmux8way_1_h), .Out(ram64_8_out));
  Multiplexer #(.select(3), .width(16), .enable("false")) multiplexer_1 (
    .in0(ram64_1_out), .in1(ram64_2_out), .in2(ram64_3_out), .in3(ram64_4_out), .in4(ram64_5_out),
    .in5(ram64_6_out), .in6(ram64_7_out), .in7(ram64_8_out), .out(Out), .sel(address[8:6]));

  // Other names for the same wires on the sheet: Address_t[5:0] = address[5:0]; adress1[2:0] = address[8:6];
  //   Clock = in_2
endmodule

module RAM4K (
  input  [15:0] In,
  input  in_2,
  input  [11:0] address,
  input  load,
  output [15:0] Out
);

  wire dmux8way_1_a, dmux8way_1_b, dmux8way_1_c, dmux8way_1_d, dmux8way_1_e, dmux8way_1_f, dmux8way_1_g,
       dmux8way_1_h;
  wire [15:0] ram512_1_out, ram512_2_out, ram512_3_out, ram512_4_out, ram512_5_out, ram512_6_out,
       ram512_7_out, ram512_8_out;

  DMux8Way dmux8way_1 (
    .in(load), .sel(address[11:9]), .a(dmux8way_1_a), .b(dmux8way_1_b), .c(dmux8way_1_c), .d(dmux8way_1_d),
    .e(dmux8way_1_e), .f(dmux8way_1_f), .g(dmux8way_1_g), .h(dmux8way_1_h));
  RAM512 ram512_1 (.In(In), .in_2(in_2), .address(address[8:0]), .load(dmux8way_1_a), .Out(ram512_1_out));
  RAM512 ram512_2 (.In(In), .in_2(in_2), .address(address[8:0]), .load(dmux8way_1_b), .Out(ram512_2_out));
  RAM512 ram512_3 (.In(In), .in_2(in_2), .address(address[8:0]), .load(dmux8way_1_c), .Out(ram512_3_out));
  RAM512 ram512_4 (.In(In), .in_2(in_2), .address(address[8:0]), .load(dmux8way_1_d), .Out(ram512_4_out));
  RAM512 ram512_5 (.In(In), .in_2(in_2), .address(address[8:0]), .load(dmux8way_1_e), .Out(ram512_5_out));
  RAM512 ram512_6 (.In(In), .in_2(in_2), .address(address[8:0]), .load(dmux8way_1_f), .Out(ram512_6_out));
  RAM512 ram512_7 (.In(In), .in_2(in_2), .address(address[8:0]), .load(dmux8way_1_g), .Out(ram512_7_out));
  RAM512 ram512_8 (.In(In), .in_2(in_2), .address(address[8:0]), .load(dmux8way_1_h), .Out(ram512_8_out));
  Multiplexer #(.select(3), .width(16), .enable("false")) multiplexer_1 (
    .in0(ram512_1_out), .in1(ram512_2_out), .in2(ram512_3_out), .in3(ram512_4_out), .in4(ram512_5_out),
    .in5(ram512_6_out), .in6(ram512_7_out), .in7(ram512_8_out), .out(Out), .sel(address[11:9]));

  // Other names for the same wires on the sheet: Address_t[8:0] = address[8:0]; adress1[2:0] = address[11:9];
  //   Clock = in_2
endmodule

module RAM16K (
  input  [15:0] In,
  input  in_2,
  input  [13:0] address,
  input  load,
  output [15:0] Out
);

  wire demultiplexer_1_out0, demultiplexer_1_out1, demultiplexer_1_out2, demultiplexer_1_out3;
  wire [15:0] ram4k_1_out, ram4k_2_out, ram4k_3_out, ram4k_4_out;

  Demultiplexer #(.select(2), .enable("false")) demultiplexer_1 (
    .out0(demultiplexer_1_out0), .out1(demultiplexer_1_out1), .out2(demultiplexer_1_out2),
    .out3(demultiplexer_1_out3), .in(load), .sel(address[13:12]));
  RAM4K ram4k_1 (.In(In), .in_2(in_2), .address(address[11:0]), .load(demultiplexer_1_out0), .Out(ram4k_1_out));
  RAM4K ram4k_2 (.In(In), .in_2(in_2), .address(address[11:0]), .load(demultiplexer_1_out1), .Out(ram4k_2_out));
  RAM4K ram4k_3 (.In(In), .in_2(in_2), .address(address[11:0]), .load(demultiplexer_1_out2), .Out(ram4k_3_out));
  RAM4K ram4k_4 (.In(In), .in_2(in_2), .address(address[11:0]), .load(demultiplexer_1_out3), .Out(ram4k_4_out));
  Multiplexer #(.select(2), .width(16), .enable("false")) multiplexer_1 (
    .in0(ram4k_1_out), .in1(ram4k_2_out), .in2(ram4k_3_out), .in3(ram4k_4_out), .out(Out),
    .sel(address[13:12]));

  // Other names for the same wires on the sheet: Address_t[11:0] = address[11:0]; adress1[1:0] = address[13:12];
  //   Clock = in_2
endmodule
