// Logisim project Not16.circ as structural Verilog
module NOt16 (
  input  [15:0] in,
  output [15:0] out
);

  not not_1 (out[0], in[0]);
  not not_2 (out[1], in[1]);
  not not_3 (out[2], in[2]);
  not not_4 (out[3], in[3]);
  not not_5 (out[4], in[4]);
  not not_6 (out[5], in[5]);
  not not_7 (out[6], in[6]);
  not not_8 (out[7], in[7]);
  not not_9 (out[8], in[8]);
  not not_10 (out[9], in[9]);
  not not_11 (out[10], in[10]);
  not not_12 (out[11], in[11]);
  // NOT_Gate not_13 has open pins: in=in[12], out=open
  // NOT_Gate not_14 has open pins: in=in[13], out=open
  // NOT_Gate not_15 has open pins: in=in[14], out=open
  // NOT_Gate not_16 has open pins: in=in[15], out=open
endmodule
