// Logisim project Mux8Way16.circ as structural Verilog: 1 circuit, main circuit main
module main (
  input  [15:0] in_1,
  input  [15:0] in_2,
  input  [15:0] in_3,
  input  [15:0] in_4,
  input  [15:0] in_5,
  input  [15:0] in_6,
  input  [2:0] in_7,
  input  [15:0] in_8,
  input  [15:0] in_9,
  output [15:0] out_10
);

  Multiplexer #(.select(3), .width(16)) multiplexer_1 (
    .in0(in_1), .in1(in_2), .in2(in_3), .in3(in_4), .in4(in_5), .in5(in_6), .in6(in_8), .in7(in_9),
    .out(out_10), .sel(in_7));  // open: en
endmodule
