// Logisim project Nand.circ as structural Verilog: 3 circuits, main circuit AndSebas
module AndSebas (
  input  a,
  input  b,
  output out
);

  wire nand_1_out;

  nand nand_1 (nand_1_out, a, a, b);
  not not_1 (out, nand_1_out);
endmodule

module Orsebas (
  input  in_1,
  output out_2
);

  nand nand_1 (out_2, in_1, in_1);
endmodule

module Xorsebas (
  input  a,
  input  b,
  output out
);

  wire and_1_out, and_2_out, not_1_out, not_2_out;

  not not_1 (not_1_out, a);
  not not_2 (not_2_out, b);
  and and_1 (and_1_out, not_1_out, b);
  and and_2 (and_2_out, a, not_2_out);
  or or_1 (out, and_1_out, and_2_out);
endmodule
