// Logisim project RAM8.circ as structural Verilog: 1 circuit, main circuit main
module main (
  input  [7:0] in_1,
  input  in_2,
  input  [7:0] in_3,
  input  clock,
  output [7:0] out_5
);

  wire not_1_out;

  assign out_5 = in_2 ? in_1 : 8'bz;  // Controlled_Buffer controlled_buffer_1
  not not_1 (not_1_out, in_2);
  RAM ram_1 (.addr(in_3), .data(out_5), .clk(clock), .ld(not_1_out));  // open: sel, clr
endmodule
