// Logisim project Register16.circ as structural Verilog: 1 circuit, main circuit main
module main (
  input  [15:0] in_1,
  input  in_2,
  output [15:0] out_3
);

  wire clock;

  Clock clock_1 (.out(clock));
  D_Flip_Flop d_ff_1 (.clk(clock), .D(in_1[0]), .Q(out_3[0]), .en(in_2));  // open: Qn, preset, reset
  D_Flip_Flop d_ff_2 (.clk(clock), .D(in_1[1]), .Q(out_3[1]), .en(in_2));  // open: Qn, preset, reset
  D_Flip_Flop d_ff_3 (.clk(clock), .D(in_1[2]), .Q(out_3[2]), .en(in_2));  // open: Qn, preset, reset
  D_Flip_Flop d_ff_4 (.clk(clock), .D(in_1[3]), .Q(out_3[3]), .en(in_2));  // open: Qn, preset, reset
  D_Flip_Flop d_ff_5 (.clk(clock), .D(in_1[4]), .Q(out_3[4]), .en(in_2));  // open: Qn, preset, reset
  D_Flip_Flop d_ff_6 (.clk(clock), .D(in_1[5]), .Q(out_3[5]), .en(in_2));  // open: Qn, preset, reset
  D_Flip_Flop d_ff_7 (.clk(clock), .D(in_1[6]), .Q(out_3[6]), .en(in_2));  // open: Qn, preset, reset
  D_Flip_Flop d_ff_8 (.clk(clock), .D(in_1[7]), .Q(out_3[7]), .en(in_2));  // open: Qn, preset, reset
  D_Flip_Flop d_ff_9 (.clk(clock), .D(in_1[8]), .Q(out_3[8]), .en(in_2));  // open: Qn, preset, reset
  D_Flip_Flop d_ff_10 (.clk(clock), .D(in_1[9]), .Q(out_3[9]), .en(in_2));  // open: Qn, preset, reset
  D_Flip_Flop d_ff_11 (.clk(clock), .D(in_1[10]), .Q(out_3[10]), .en(in_2));  // open: Qn, preset, reset
  D_Flip_Flop d_ff_12 (.clk(clock), .D(in_1[11]), .Q(out_3[11]), .en(in_2));  // open: Qn, preset, reset
  D_Flip_Flop d_ff_13 (.clk(clock), .D(in_1[12]), .Q(out_3[12]), .en(in_2));  // open: Qn, preset, reset
  D_Flip_Flop d_ff_14 (.clk(clock), .D(in_1[13]), .Q(out_3[13]), .en(in_2));  // open: Qn, preset, reset
  D_Flip_Flop d_ff_15 (.clk(clock), .D(in_1[14]), .Q(out_3[14]), .en(in_2));  // open: Qn, preset, reset
  D_Flip_Flop d_ff_16 (.clk(clock), .D(in_1[15]), .Q(out_3[15]), .en(in_2));  // open: Qn, preset, reset

  // Other names for the same wires on the sheet: load = in_2
endmodule
